# Fritzing sketch Battery Status (saved by Fritzing 0.9.4)
breadboards: 1

parts:
  Part1 = FTDI Basic Programmer
  C1 = Electrolytic Capacitor [capacitance=1µF package="100 mil [THT, electrolytic]"]
  R1 = Resistor [tolerance=±5% resistance=10k package=THT]
  R2 = Resistor [tolerance=±5% resistance=10k package=THT]
  S1 = Pushbutton [package="[THT]"]
  S2 = Pushbutton [package="[THT]"]
  C2 = Capacitor [package=cap-pth-small2]
  R3 = Resistor [tolerance=±5% resistance=10k package=THT]
  U2 = ESP8266 WiFi Module [part_number=ESP8266]
  U3 = ESP8266 WiFi Module [part_number=ESP8266]  # not connected
  BAT1 = Battery Holders [package=battery-aa]
  R4 = Resistor [tolerance=±5% resistance=220 package=THT]
  R5 = Resistor [tolerance=±5% resistance=220 package=THT]
  Onderdeel1 = TP4056 Charger
  C3 = Capacitor [package=cap-pth-small2]
  C4 = Electrolytic Capacitor [capacitance=1µF package="100 mil [THT, electrolytic]"]
  DS1 = DS18B20 1-Wire Temperature Sensor [part_number=DS18B20]

nets:
  N1: Part1.RXI, U2.TXD
  N2: Part1.TXO, U2.RXD
  VCC: Part1.POWER, C1.+, R1.Pin_1, R2.Pin_1, C2.2, R3.Pin_0, U2.VCC, C3.2, C4.+, DS1.VDD
  GND: Part1.GND, C1.-, S1.Pin_3, S1.Pin_4, S2.Pin_3, S2.Pin_4, C2.1, U2.GND, U2.GPIO_15, BAT1.-, R4.Pin_0, Onderdeel1.BAT-, C3.1, C4.-, DS1.GND
  N3: R1.Pin_0, S1.Pin_1, S1.Pin_2, U2.GPIO_0
  N4: R2.Pin_0, S2.Pin_1, S2.Pin_2, U2.REST
  N5: R3.Pin_1, U2.CH_PD
  N6: U2.ADC_0, R4.Pin_1, R5.Pin_0
  N7: BAT1.+, R5.Pin_1, Onderdeel1.IN+, Onderdeel1.BAT+, DS1.DQ

notes:
  PROGRAM
  RESET
  https://www.studiopieters.nl
  RST
  ADC
  CH_PD
  GPIO16
  GPIO14
  GPIO12
  GPIO13
  VCC
  TXD
  GPIO4
  GPIO0
  GPIO5
  GPIO15
  GPIO2
  GND
  CS0
  MOSI
  GPIO10
  GPIO9
  SCLK
  MISO
  2.7KΩ
  10KΩ
  TP4056 Charger
  █
  100nf
  100μF
  MCP1700

custom parts:
  FTDI Basic Programmer: Description: This is the newest revision of our FTDI Basic. We now use a SMD 6-pin header on the bottom, which makes it smaller and more compact. Functionality has remained the same. This is a basic breakout board for the FTDI FT232RL USB to serial IC. The pinout of this board matches the FTDI cable to work with official Arduino and cloned 3.3V Arduino boards. It can also be used for general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
  ESP8266 WiFi Module: Generic WiFi Module based on the ESP8266 with onboard PCB antenna and UART communications
  Battery Holders: Battery Holders Various common sizes : AA, AAA, 20mm coin cell and 12mm coin cell.
